# Fritzing sketch GasDetector (saved by Fritzing 0.9.3b)

parts:
  Composant1 = Arduino Nano (Rev3.0)
  DHT1 = DHT11 Humitidy and Temperature Sensor
  Composant3 = MQ-4
  Squix1 = OLED 0.96" 128x64 I2C SSD1306
  R1 = Resistor [tolerance=±5% resistance=10k package=THT]

nets:
  GND: Composant1.GND, DHT1.GND, Composant3.GND, Squix1.GND
  N1: Composant1.D2, DHT1.DATA, R1.Pin_0
  VCC: Composant1.5V, DHT1.VDD, Composant3.VCC, Squix1.VCC, R1.Pin_1
  N2: Composant1.A5, Squix1.SCL
  N3: Composant1.A4, Squix1.SCA
  N4: Composant1.A0, Composant3.AO

custom parts:
  DHT11 Humitidy and Temperature Sensor: DHT11 Humidity and Temperature Sensor
